# Fritzing sketch DHT22_ESP (saved by Fritzing 0.9.3b)
breadboards: 1

parts:
  Part1 = Adafruit Feather HUZZAH ESP8266 [part_number="Adafruit #2821"]
  RHT1 = Humidity and Temperature Sensor RHT03
  R1 = Resistor [tolerance=±5% resistance=220 package="2010 [SMD]"]

nets:
  N1: Part1.GPIO14/SCK, RHT1.Data-signal, R1.Pin_0
  N2: RHT1.Vcc, R1.Pin_1

notes:
  C7 and R3 are not necessary, but they smooth the reported values a lot.
  You can try without, just connect ADC between R1 and R2

custom parts:
  Adafruit Feather HUZZAH ESP8266: his is the Adafruit Feather HUZZAH ESP8266 - our take on an 'all-in-one' ESP8266 WiFi development board with built in USB and battery charging. Its an ESP8266 WiFi module with all the extras you need, ready to rock! We have other boards in the Feather family, check'em out here. At the Feather HUZZAH's heart is an ESP8266 WiFi microcontroller clocked at 80 MHz and at 3.3V logic. This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

// code stored in the sketch: main.ino
void setup() {
	// do your stuff, like setup WiFi
}

void loop() {

	int rawLevel = analogRead(A0);

	// the 10k?/47k? voltage divider reduces the voltage, so the ADC Pin can handle it
	// According to Wolfram Alpha, this results in the following values:
  // 10k?/(47k?+10k?)*  5v = 0.8772v
  // 10k?/(47k?+10k?)*3.7v = 0.649v
  // 10k?/(47k?+10k?)*3.1v = 0.544
	// * i asumed 3.1v as minimum voltage => see LiPO discharge diagrams

  // convert battery level to percent
  int level = map(rawLevel, 544, 649, 0, 100);

	// i'd like to report back the real voltage, so apply some math to get it back
	// 1. convert the ADC level to a float
	// 2. divide by (R2[1] / R1 + R2)
  // [1] the dot is a trick to handle it as float
  float realVoltage = (float)rawLevel / 1000 / (10000. / (47000 + 10000));
  
	// build a nice string to send to influxdb or whatever you like
	char dataLine[64];
  // sprintf has no support for floats, but will be added later, so we need a String() for now
  sprintf(dataLine, "voltage percent=%d,adc=%d,real=%s,charging=%d\n",
    level < 150 ? level : 100, // cap level to 100%, just for graphing, i don't want to see your lab, when the battery actually gets to that level
    rawLevel,
    String(realVoltage, 3).c_str(),
    rawLevel > 850 ? 1 : 0 // USB is connected if the reading is ~870, as the voltage will be 5V, so we assume it's charging
	);

  udp.beginPacket({192, 168, 1, 1}, 8089);
  udp.print(dataLine);
  udp.endPacket();

  delay(1000);
}
