# Fritzing sketch GSM_Tracker (saved by Fritzing 0.9.3b)
breadboards: 1

parts:
  RHT1 = Humidity and Temperature Sensor RHT03
  Part1 = Adafruit Feather 32u4 FONA [part_number="Adafruit #3027"]
  R1 = Resistor [tolerance=±5% resistance=220 package="2512 [SMD]"]

nets:
  VCC: RHT1.Vcc, Part1.+3V3, R1.Pin_1
  N1: RHT1.Data-signal, Part1.6_UART_RTS, R1.Pin_0
  N2: RHT1.GND_2, Part1.GND

custom parts:
  Adafruit Feather 32u4 FONA: This is the Adafruit Feather 32u4 FONA - our take on an 'all-in-one' Arduino-compatible + audio/sms/data capable cellular with built in USB and battery charging. Its an Adafruit Feather 32u4 with a FONA800 module, ready to rock! We have other boards and accessories in the Feather family, check'em out here. At the Feather 32u4's heart is at ATmega32u4 clocked at 8 MHz and at 3.3V logic, a chip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
