# Fritzing sketch LoRaWAN (saved by Fritzing 0.9.3b)
breadboards: 1

parts:
  AM1 = AM2320 Humidity and Temperature Sensor [part_number="Adafruit #3721"]
  R2 = Resistor [tolerance=±5% resistance=220 package="0603 [SMD]"]
  R3 = Resistor [tolerance=±5% resistance=220 package="2512 [SMD]"]
  Part6 = Adafruit Feather M0 RFM9x LoRa [part_number="Adafruit #3178 or #3179"]

nets:
  VDD: AM1.VDD, R2.Pin_0, R3.Pin_1, Part6.+3V3
  N1: AM1.SDA, R2.Pin_1, Part6.SDA
  GND: AM1.GND, Part6.GND
  N2: AM1.SCL, R3.Pin_0, Part6.SCL
  N3: Part6.D11, Part6.DIO2

custom parts:
  AM2320 Humidity and Temperature Sensor: AM2320 I2C Humidity and Temperature Sensor
  Adafruit Feather M0 RFM9x LoRa: This is the Adafruit Feather M0 RFM95 LoRa Radio - our take on an microcontroller with a "Long Range (LoRa)" packet radio transceiver with built in USB and battery charging. Its an Adafruit Feather M0 with a 433Mhz or 900MHz radio module cooked in! Great for making wireless networks that are more flexible than Bluetooth LE and without the high power requirements of WiFi. We have other boards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
