# Fritzing sketch M0_BLE (saved by Fritzing 0.9.3b)
breadboards: 1

parts:
  RHT1 = Humidity and Temperature Sensor RHT03
  R1 = Resistor [tolerance=±5% resistance=220 package="0402 [SMD]"]
  Part2 = adafruit [part_number="Adafruit #2995"]

nets:
  N1: RHT1.Vcc, Part2.connector42
  N2: RHT1.Data-signal, R1.Pin_1
  N3: RHT1.GND_2, Part2.connector40
  N4: R1.Pin_0, Part2.connector50
