# Fritzing sketch gps (saved by Fritzing 0.9.3b)
breadboards: 1

parts:
  Part1 = Adafruit GPS FeatherWing [part_number="Adafruit #3133"]
  Part2 = Adafruit Feather M0 WINC1500 [part_number="Adafruit #3010"]

nets:
  N1: Part1.3V, Part2.+3V3
  GND: Part1.GND, Part2.GND
  N2: Part1.RX, Part2.D1
  N3: Part1.TX, Part2.D0

custom parts:
  Adafruit GPS FeatherWing: Give your Feather a sense of place, with an Ultimate GPS FeatherWing. In 2013 we designed the Ultimate GPS module to satisfy all your GPS desires - and now we have brought its power and versatility plus more to our Feather series with the Adafruit Ultimate GPS FeatherWing! This FeatherWing plugs right into your Feather board and gives it a precise, sensitive, and low power GPS module for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
  Adafruit Feather M0 WINC1500: This is the Adafruit Feather M0 WiFi w/ATWINC1500 - our take on an 'all-in-one' Arduino-compatible + high speed, reliable WiFi with built in USB and battery charging. Its an Adafruit Feather M0 with a WiFi module, ready to rock! Connect your Feather to the Internet with this fine new FCC-certified WiFi module from Atmel. This 802.11bgn-capable WiFi module is the best new thing for networking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
